# Fritzing sketch light_saber_diagram (saved by Fritzing 0.9.8b)
breadboards: 1

parts:
  Part1 = Arduino Nano (Rev3.0)
  U1 = WS2812 RGB LED strip
  R1 = Resistor [tolerance=±20% resistance=330 power=0.25 package=THT]
  S1 = Pushbutton [package="[THT]"]
  R2 = Resistor [tolerance=±5% resistance=1k package="0603 [SMD]"]
  VCC1 = 4 x AAA Battery Mount

nets:
  GND: Part1.GND, U1.GND, R2.Pin_0, VCC1.-
  N1: Part1.D5, S1.Pin_3, S1.Pin_4, R2.Pin_1
  N2: Part1.D8, R1.Pin_1
  VIN: Part1.VIN, U1.VCC, S1.Pin_1, S1.Pin_2, VCC1.+
  N3: U1.DIN, R1.Pin_0

notes:
  Pull-down resistor. Any amount of Ohm would work, but 1KOhm is recommended
  330 Ohm resistor
  WS2812B LED strip
  4 AA (rechargeable ) 1.5v batteries
  Push button
  Arduino Nano

custom parts:
  WS2812 RGB LED strip: WS2812 strip
