# Fritzing sketch light_saber (saved by Fritzing 0.9.8b)
circuit board: 13.4417cm x 2.47342cm
breadboards: 1

parts:
  Arduino_Nano = Arduino Nano (Rev3.0)
  LED_1 = WS2812 RGB LED strip
  330_Ohm_resistor = Resistor [tolerance=±20% resistance=330 power=0.25 package=THT]
  Button = Pushbutton [package="[THT]"]
  1KOhm_resistor = Resistor [tolerance=±5% resistance=1k package="0603 [SMD]"]
  2_1mm_Barrel_female = 2.1mm Barrel Jack with Terminal Block
  LED_2 = WS2812 RGB LED strip

nets:
  GND: Arduino_Nano.GND, LED_1.GND, 1KOhm_resistor.Pin_0, 2_1mm_Barrel_female.NEG, LED_2.GND
  N1: Arduino_Nano.D5, Button.Pin_3, Button.Pin_4, 1KOhm_resistor.Pin_1
  N2: Arduino_Nano.D8, 330_Ohm_resistor.Pin_1
  VCC: Arduino_Nano.VIN, LED_1.VCC, Button.Pin_1, Button.Pin_2, 2_1mm_Barrel_female.POS, LED_2.VCC
  N3: LED_1.DIN, 330_Ohm_resistor.Pin_0, LED_2.DIN

notes:
  Arduino Nano
  Push button
  Pull-down resistor. Any amount of Ohm would work, but 1KOhm is recommended
  2 WS2812B LED strips
  330 Ohm resistor
  2.1mm Barrel jack with terminal block

custom parts:
  WS2812 RGB LED strip: WS2812 strip
